// Logisim project RISChaiddy3.circ as structural Verilog: 4 circuits, main circuit main
module main (
  input  CLK
);

  wire ALURAM, ALUZERO, CLK_t, not_1_out, RESET;
  wire [1:0] ALUOP, multiplexer_1_out, PCMODE;
  wire [3:0] ALU_output, multiplexer_2_out, multiplexer_3_out, ram_1_data, REG_File_r1out, REG_RT;
  wire [7:0] ABS, PC_out, PLAOUT;
  wire [11:8] INSTRUCTION;

  Clock clock_1 (.out(CLK));
  PC PC (.CLK(CLK_t), .ABS(ABS), .PCMODE(PCMODE), .IMM(ABS[3:0]), .RESET(RESET), .OUT(PC_out));
  ROM #(.dataWidth(12)) rom_1 (.addr(PC_out), .data({INSTRUCTION, ABS}));  // open: sel
  // PLA pla_1: pin names not known; wires that end beside it: {{4{ALUZERO}}, ABS[0], ABS[1], INSTRUCTION}, {PCMODE, ALUOP, PLAOUT[7:4], ALURAM, PLAOUT[2:0]}
  Multiplexer #(.width(2)) multiplexer_1 (
    .in0(ABS[3:2]), .in1(ABS[5:4]), .out(multiplexer_1_out), .sel(PLAOUT[6]));  // open: en
  REG_File REG_File (
    .CLK(CLK_t), .IN(multiplexer_3_out), .WEN(PLAOUT[7]), .WIN(multiplexer_1_out), .R1IN(ABS[7:6]),
    .R2IN(ABS[5:4]), .R1OUT(REG_File_r1out), .R2OUT(REG_RT));
  Multiplexer #(.width(4)) multiplexer_2 (
    .in0(REG_RT), .in1(ABS[3:0]), .out(multiplexer_2_out), .sel(PLAOUT[5]));  // open: en
  ALU ALU (.A(REG_File_r1out), .zero(ALUZERO), .B(multiplexer_2_out), .Operation(ALUOP), .Output(ALU_output));
  not not_1 (not_1_out, PLAOUT[4]);
  RAM #(.addrWidth(4), .dataWidth(4), .bus("separate")) ram_1 (
    .addr(ALU_output), .din(REG_RT), .data(ram_1_data), .str(not_1_out), .clk(CLK_t));  // open: sel, ld, clr
  Multiplexer #(.width(4)) multiplexer_3 (
    .in0(ALU_output), .in1(ram_1_data), .out(multiplexer_3_out), .sel(ALURAM));  // open: en
  // also tied to GND on the sheet: ALUZERO

  // Other names for the same wires on the sheet: OPCODE[3:0] = INSTRUCTION; FUNC[1:0] = ABS[1:0]; IMM[3:0] = ABS[3:0];
  //   INSTRUCTION[7:0] = ABS; RD[1:0] = ABS[3:2]; RT[1:0] = ABS[5:4]; RS[1:0] = ABS[7:6];
  //   PLAOUT (some bits) = {PCMODE, ALUOP, ALURAM}; WRAM = PLAOUT[4]; RTIMM = PLAOUT[5]; RDRT = PLAOUT[6];
  //   WEN = PLAOUT[7]
endmodule

module PC (
  input  CLK,
  input  [7:0] ABS,
  input  [1:0] PCMODE,
  input  [3:0] IMM,
  input  RESET,
  output [7:0] OUT
);

  wire [7:0] adder_1_out, adder_2_out, bit_extender_1_out, multiplexer_1_out;

  Multiplexer #(.select(2), .width(8)) multiplexer_1 (
    .in0(adder_1_out), .in1(adder_2_out), .in2(ABS), .out(multiplexer_1_out), .sel(PCMODE));  // open: in3, en
  Register #(.trigger("falling")) PR (.D(multiplexer_1_out), .Q(OUT), .clk(CLK), .clr(RESET));  // open: en
  Adder adder_1 (.a(OUT), .b(8'h1), .out(adder_1_out));  // open: cin, cout
  assign bit_extender_1_out = {{4{IMM[3]}}, IMM};  // Bit_Extender bit_extender_1
  Adder adder_2 (.a(adder_1_out), .b(bit_extender_1_out), .out(adder_2_out));  // open: cin, cout
endmodule

module REG_File (
  input  CLK,
  input  [3:0] IN,
  input  WEN,
  input  [1:0] WIN,
  input  [1:0] R1IN,
  input  [1:0] R2IN,
  output [3:0] R1OUT,
  output [3:0] R2OUT
);

  wire and_1_out, and_2_out, and_3_out, and_4_out, decoder_1_out0, decoder_1_out1, decoder_1_out2,
       decoder_1_out3;
  wire [3:0] R0_q, R1_q, R2_q, R3_q;

  Decoder #(.select(2)) decoder_1 (
    .out0(decoder_1_out0), .out1(decoder_1_out1), .out2(decoder_1_out2), .out3(decoder_1_out3), .sel(WIN));  // open: en
  and and_1 (and_1_out, WEN, decoder_1_out0);
  and and_2 (and_2_out, WEN, decoder_1_out1);
  and and_3 (and_3_out, WEN, decoder_1_out2);
  and and_4 (and_4_out, WEN, decoder_1_out3);
  Register #(.width(4), .trigger("falling")) R0 (.D(IN), .en(and_1_out), .Q(R0_q), .clk(CLK));  // open: clr
  Register #(.width(4), .trigger("falling")) R1 (.D(IN), .en(and_2_out), .Q(R1_q), .clk(CLK));  // open: clr
  Register #(.width(4), .trigger("falling")) R2 (.D(IN), .en(and_3_out), .Q(R2_q), .clk(CLK));  // open: clr
  Register #(.width(4), .trigger("falling")) R3 (.D(IN), .en(and_4_out), .Q(R3_q), .clk(CLK));  // open: clr
  Multiplexer #(.select(2), .width(4)) multiplexer_1 (
    .in0(R0_q), .in1(R1_q), .in2(R2_q), .in3(R3_q), .out(R1OUT), .sel(R1IN));  // open: en
  Multiplexer #(.select(2), .width(4)) multiplexer_2 (
    .in0(R0_q), .in1(R1_q), .in2(R2_q), .in3(R3_q), .out(R2OUT), .sel(R2IN));  // open: en
endmodule

module ALU (
  input  [3:0] A,
  input  [3:0] B,
  input  [1:0] Operation,
  output [3:0] Output,
  output zero
);

  wire subtractor_1_bout;
  wire [3:0] adder_1_out, bit_extender_1_out, subtractor_1_out;

  Adder #(.width(4)) adder_1 (.a(A), .b(B), .out(adder_1_out));  // open: cin, cout
  Subtractor #(.width(4)) subtractor_1 (.a(A), .b(B), .out(subtractor_1_out), .bout(subtractor_1_bout));  // open: bin
  assign bit_extender_1_out = {{3{1'b0}}, subtractor_1_bout};  // Bit_Extender bit_extender_1
  Multiplexer #(.select(2), .width(4), .enable("false")) multiplexer_1 (
    .in0(adder_1_out), .in1(subtractor_1_out), .in2(bit_extender_1_out), .in3(B), .out(Output),
    .sel(Operation));
  Comparator #(.width(4)) comparator_1 (.a(Output), .b(4'b0000), .eq(zero));  // open: gt, lt
endmodule
